# Fritzing sketch WeatherStation (saved by Fritzing 0.9.2b)
circuit board: 7.94184cm x 4.81766cm
breadboards: 1

parts:
  Arduino_Pro_Mini = Arduino Pro Mini v13
  LLC_3_3V_/_5_0V = Logic Level Converter
  C1 = Ceramic Capacitor [capacitance=100nF package="200 mil [THT, multilayer]"]
  5_0V = Power plug
  R1 = Resistor [tolerance=±5% resistance=330 package=THT]
  R3 = Resistor [tolerance=±5% resistance=10k package=THT]
  R2 = Resistor [tolerance=±5% resistance=560 package=THT]
  LM317T = Voltage Regulator - Variable [package="TO220 [THT]"]
  C2 = Electrolytic Capacitor [capacitance=1μF package="0405 [SMD, electrolytic]"]
  WiFi_LED = DUO LED RG [package="5 mm [THT]"]
  R4 = Resistor [tolerance=±5% resistance=560 package=THT]
  R5 = Resistor [tolerance=±5% resistance=560 package=THT]
  DHT22 = DHT22 Humidity and Temperature Sensor
  R6 = Resistor [tolerance=±5% resistance=3.3k package=THT]
  R7 = Resistor [tolerance=±5% resistance=3.3k package=THT]
  part = ESP8266 ESP01 [part_number=ESP8266 package=THT]

nets:
  N1: Arduino_Pro_Mini.D0/TX, LLC_3_3V_/_5_0V.TX_HV
  N2: Arduino_Pro_Mini.D1/RX, LLC_3_3V_/_5_0V.RX_HV
  5V: Arduino_Pro_Mini.VCC, LLC_3_3V_/_5_0V.HV, C1.1, 5_0V.VCC, R3.Pin_1, LM317T.IN, DHT22.VDD
  GND: Arduino_Pro_Mini.GND, LLC_3_3V_/_5_0V.GND, C1.0, 5_0V.GND, R2.Pin_1, C2.-, WiFi_LED.common_cathode, DHT22.GND, part.GND
  N3: Arduino_Pro_Mini.D9_PWM, R3.Pin_0, DHT22.DATA
  N4: Arduino_Pro_Mini.D8, R5.Pin_0
  N5: Arduino_Pro_Mini.D7, R4.Pin_0
  N6: Arduino_Pro_Mini.D3_PWM, LLC_3_3V_/_5_0V.TX2_HV
  N7: Arduino_Pro_Mini.D2, LLC_3_3V_/_5_0V.RX2_HV
  N8: LLC_3_3V_/_5_0V.TX2_LV, R7.Pin_1, part.GPIO16
  N9: LLC_3_3V_/_5_0V.RX2_LV, R6.Pin_1, part.CH_PD
  3.3V: LLC_3_3V_/_5_0V.LV, R1.Pin_1, LM317T.OUT, C2.+, R6.Pin_0, R7.Pin_0, part.VCC
  N10: LLC_3_3V_/_5_0V.RX_LV, part.TXD
  N11: LLC_3_3V_/_5_0V.TX_LV, part.RXD
  N12: R1.Pin_0, R2.Pin_0, LM317T.ADJ
  N13: WiFi_LED.red_anode, R4.Pin_1
  N14: WiFi_LED.green_anode, R5.Pin_1

notes:
  5V@1A (±5%)
  Regulated Power Supply
  Temperature:
  -40 - 80°C, ±0.5°C
  Humidity:
  0-100%, ±2%

custom parts:
  ESP8266 ESP01: Generic WiFi Module based on the ESP8266 with onboard PCB antenna and UART communications
